// Logisim project TN1.circ as structural Verilog: 1 circuit, main circuit main
module main (
  input  A,
  input  B,
  input  C,
  output AND,
  output NOT,
  output OR,
  output NAND,
  output CHAIN,
  output NOR,
  output XOR,
  output XNOR,
  output XOR3,
  output NAND3
);

  not not_1 (NOT, A);
  and and_1 (AND, A, B);
  or or_1 (OR, B, A);
  nand nand_1 (NAND, B, A);
  nor nor_1 (NOR, B, A);
  xor xor_1 (XOR, B, A);
  xnor xnor_1 (XNOR, B, A);
  ExactlyOne xor_2 (.out(XOR3), .in0(C), .in2(B), .in4(A));
  nand nand_2 (NAND3, C, B, A);
  nand nand_3 (CHAIN, NAND, C);
endmodule
