// Logisim project TN4.circ as structural Verilog: 1 circuit, main circuit main
module main (
  input  A,
  input  B,
  input  C,
  input  D,
  output F_can,
  output F_sop,
  output F_pos
);

  wire and_1_out, and_2_out, and_3_out, and_4_out, and_5_out, and_6_out, and_7_out, and_8_out, and_9_out,
       not_1_out, not_2_out, not_3_out, not_4_out, not_5_out, not_6_out, not_7_out, not_8_out, not_9_out,
       not_10_out, not_11_out, not_12_out, not_13_out, not_14_out, not_15_out, not_16_out, or_1_out,
       or_2_out, or_3_out, or_4_out;

  not not_1 (not_1_out, A);
  not not_2 (not_2_out, B);
  not not_3 (not_3_out, A);
  not not_4 (not_4_out, C);
  not not_5 (not_5_out, A);
  not not_6 (not_6_out, B);
  not not_7 (not_7_out, C);
  not not_8 (not_8_out, A);
  not not_9 (not_9_out, A);
  not not_10 (not_10_out, C);
  not not_11 (not_11_out, B);
  not not_12 (not_12_out, C);
  not not_13 (not_13_out, D);
  not not_14 (not_14_out, A);
  not not_15 (not_15_out, B);
  not not_16 (not_16_out, C);
  and and_1 (and_1_out, not_1_out, not_2_out, C, D);
  and and_2 (and_2_out, not_3_out, B, not_4_out, D);
  and and_3 (and_3_out, not_5_out, B, C, D);
  and and_4 (and_4_out, A, not_6_out, C, D);
  and and_5 (and_5_out, A, B, not_7_out, D);
  and and_6 (and_6_out, not_8_out, C, D);
  and and_7 (and_7_out, not_9_out, B, D);
  and and_8 (and_8_out, B, not_10_out, D);
  and and_9 (and_9_out, not_11_out, C, D);
  or or_1 (or_1_out, C, D);
  or or_2 (or_2_out, not_12_out, D);
  or or_3 (or_3_out, B, C, not_13_out);
  or or_4 (or_4_out, not_14_out, not_15_out, not_16_out);
  or or_5 (F_can, and_1_out, and_2_out, and_3_out, and_4_out, and_5_out);
  or or_6 (F_sop, and_6_out, and_7_out, and_8_out, and_9_out);
  and and_10 (F_pos, or_1_out, or_2_out, or_3_out, or_4_out);
endmodule
